# Fritzing sketch wiring_diagram_leonardo (saved by Fritzing 0.9.6b)
breadboards: 1

parts:
  Bauteil1 = Arduino Leonardo (Rev3b)
  range = Momentary Switch [package=ksa_sealed_tac_switch]
  splitter = Momentary Switch [package=ksa_sealed_tac_switch]
  comfort_shift = Momentary Switch [package=ksa_sealed_tac_switch]
  R1 = Resistor [tolerance=±5% power=0.25 resistance=10k package=THT]
  R2 = Resistor [tolerance=±5% power=0.25 resistance=10k package=THT]
  R3 = Resistor [tolerance=±5% power=0.25 resistance=10k package=THT]

nets:
  N1: Bauteil1.D0/RX, comfort_shift.1, comfort_shift.2, R3.Pin_0
  N2: Bauteil1.D1/TX, splitter.1, splitter.2, R2.Pin_0
  N3: Bauteil1.D2/SDA, Bauteil1.SDA, range.1, range.2, R1.Pin_0
  N4: Bauteil1.5V, R1.Pin_1, R2.Pin_1, R3.Pin_1
  N5: Bauteil1.GND, range.3, range.4, splitter.3, splitter.4, comfort_shift.3, comfort_shift.4
