# Fritzing sketch wiring_diagram_promicro (saved by Fritzing 0.9.6b)
breadboards: 1

parts:
  range = Momentary Switch [package=ksa_sealed_tac_switch]
  splitter = Momentary Switch [package=ksa_sealed_tac_switch]
  comfort_shift = Momentary Switch [package=ksa_sealed_tac_switch]
  Bauteil2 = Arduino Pro Micro (Clone)

nets:
  N1: range.1, range.2, Bauteil2.A2
  N2: range.3, range.4, splitter.3, splitter.4, comfort_shift.3, comfort_shift.4, Bauteil2.GND
  N3: splitter.1, splitter.2, Bauteil2.A1
  N4: comfort_shift.1, comfort_shift.2, Bauteil2.A0
